// Logisim project Automat_bancar.circ as structural Verilog: 17 circuits, main circuit main
module main (
  input  in_1,
  input  in_2,
  input  in_3,
  input  in_4,
  input  in_5,
  input  in_6,
  input  in_7,
  input  in_8,
  input  in_9,
  input  in_10,
  input  in_11,
  input  in_12,
  input  in_13,
  input  in_14,
  input  in_15
);

  wire bancomat_1_fail, bancomat_1_finish, button_1_out, button_2_out, button_3_out, button_4_out,
       clock_1_out;
  wire [6:0] bancomat_1_out_24, enable_afisor_1_out_3, enable_afisor_2_out_3, enable_afisor_3_out_3,
       enable_afisor_4_out_3, enable_afisor_5_out_3, enable_afisor_6_out_3, enable_afisor_7_out_3,
       enable_afisor_8_out_3;
  wire [7:0] bancomat_1_out_23;

  enable_afisor enable_afisor_1 (.in_2(bancomat_1_out_23[7]), .out_3(enable_afisor_1_out_3), .in_1(bancomat_1_out_24));
  Button button_1 (.out(button_1_out));
  Clock clock_1 (.out(clock_1_out));
  Button button_2 (.out(button_2_out));
  Button button_3 (.out(button_3_out));
  Button button_4 (.out(button_4_out));
  enable_afisor enable_afisor_2 (.in_2(bancomat_1_out_23[6]), .out_3(enable_afisor_2_out_3), .in_1(bancomat_1_out_24));
  _7_Segment_Display u_7_segment_display_1 (
    .g(enable_afisor_1_out_3[6]), .f(enable_afisor_1_out_3[5]), .a(enable_afisor_1_out_3[0]),
    .b(enable_afisor_1_out_3[1]), .e(enable_afisor_1_out_3[4]), .d(enable_afisor_1_out_3[3]),
    .c(enable_afisor_1_out_3[2]));  // open: dp
  _7_Segment_Display u_7_segment_display_2 (
    .g(enable_afisor_2_out_3[6]), .f(enable_afisor_2_out_3[5]), .a(enable_afisor_2_out_3[0]),
    .b(enable_afisor_2_out_3[1]), .e(enable_afisor_2_out_3[4]), .d(enable_afisor_2_out_3[3]),
    .c(enable_afisor_2_out_3[2]));  // open: dp
  enable_afisor enable_afisor_3 (.in_2(bancomat_1_out_23[5]), .out_3(enable_afisor_3_out_3), .in_1(bancomat_1_out_24));
  _7_Segment_Display u_7_segment_display_3 (
    .g(enable_afisor_3_out_3[6]), .f(enable_afisor_3_out_3[5]), .a(enable_afisor_3_out_3[0]),
    .b(enable_afisor_3_out_3[1]), .e(enable_afisor_3_out_3[4]), .d(enable_afisor_3_out_3[3]),
    .c(enable_afisor_3_out_3[2]));  // open: dp
  enable_afisor enable_afisor_4 (.in_2(bancomat_1_out_23[4]), .out_3(enable_afisor_4_out_3), .in_1(bancomat_1_out_24));
  enable_afisor enable_afisor_5 (.in_2(bancomat_1_out_23[3]), .out_3(enable_afisor_5_out_3), .in_1(bancomat_1_out_24));
  _7_Segment_Display u_7_segment_display_4 (
    .g(enable_afisor_4_out_3[6]), .f(enable_afisor_4_out_3[5]), .a(enable_afisor_4_out_3[0]),
    .b(enable_afisor_4_out_3[1]), .e(enable_afisor_4_out_3[4]), .d(enable_afisor_4_out_3[3]),
    .c(enable_afisor_4_out_3[2]));  // open: dp
  _7_Segment_Display u_7_segment_display_5 (
    .g(enable_afisor_5_out_3[6]), .f(enable_afisor_5_out_3[5]), .a(enable_afisor_5_out_3[0]),
    .b(enable_afisor_5_out_3[1]), .e(enable_afisor_5_out_3[4]), .d(enable_afisor_5_out_3[3]),
    .c(enable_afisor_5_out_3[2]));  // open: dp
  BANCOMAT bancomat_1 (
    .reset(button_2_out), .in_17(button_1_out), .confirm(button_3_out), .out_23(bancomat_1_out_23),
    .next(button_4_out), .out_24(bancomat_1_out_24), .in_1(in_1), .in_2(in_2), .s(in_3), .z(in_4), .u(in_5),
    ._500(in_6), ._200(in_7), ._100(in_8), ._50(in_9), ._10(in_10), ._5(in_11), .p3(in_12), .p2(in_13),
    .p1(in_14), .p0(in_15), .finish(bancomat_1_finish), .fail(bancomat_1_fail), .in_19(clock_1_out));
  LED led_1 (.in(bancomat_1_finish));
  LED led_2 (.in(bancomat_1_fail));
  enable_afisor enable_afisor_6 (.in_2(bancomat_1_out_23[2]), .out_3(enable_afisor_6_out_3), .in_1(bancomat_1_out_24));
  _7_Segment_Display u_7_segment_display_6 (
    .g(enable_afisor_6_out_3[6]), .f(enable_afisor_6_out_3[5]), .a(enable_afisor_6_out_3[0]),
    .b(enable_afisor_6_out_3[1]), .e(enable_afisor_6_out_3[4]), .d(enable_afisor_6_out_3[3]),
    .c(enable_afisor_6_out_3[2]));  // open: dp
  enable_afisor enable_afisor_7 (.in_2(bancomat_1_out_23[1]), .out_3(enable_afisor_7_out_3), .in_1(bancomat_1_out_24));
  enable_afisor enable_afisor_8 (.in_2(bancomat_1_out_23[0]), .out_3(enable_afisor_8_out_3), .in_1(bancomat_1_out_24));
  _7_Segment_Display u_7_segment_display_7 (
    .g(enable_afisor_7_out_3[6]), .f(enable_afisor_7_out_3[5]), .a(enable_afisor_7_out_3[0]),
    .b(enable_afisor_7_out_3[1]), .e(enable_afisor_7_out_3[4]), .d(enable_afisor_7_out_3[3]),
    .c(enable_afisor_7_out_3[2]));  // open: dp
  _7_Segment_Display u_7_segment_display_8 (
    .g(enable_afisor_8_out_3[6]), .f(enable_afisor_8_out_3[5]), .a(enable_afisor_8_out_3[0]),
    .b(enable_afisor_8_out_3[1]), .e(enable_afisor_8_out_3[4]), .d(enable_afisor_8_out_3[3]),
    .c(enable_afisor_8_out_3[2]));  // open: dp

  // Notes on the sheet:
  //   00-INTEROGARE
  //   01-DEPUNERE
  //   10-RETRAGERE
  //   11-TRANSFER
endmodule

module inputPIN (
  input  in_1,
  input  in_2,
  input  in_3,
  input  in_4,
  input  confirm,
  input  enable,
  output [3:0] out_7,
  output [15:0] out_8
);

  wire counter_1_q, not_1_out;
  wire [15:0] pin_cod_1_out_2;

  not not_1 (not_1_out, enable);
  Counter #(.width(1), .max('h1), .ongoal("stay")) counter_1 (
    .count(confirm), .Q(counter_1_q), .clk(confirm), .clr(not_1_out));  // open: load, D, carry
  Register #(.width(4)) register_1 (
    .D({in_1, in_2, in_3, in_4}), .en(1'b1), .Q(out_7), .clk(counter_1_q));  // open: clr
  pin_cod pin_cod_1 (.in_1({in_1, in_2, in_3, in_4}), .out_2(pin_cod_1_out_2));
  assign out_8 = enable ? pin_cod_1_out_2 : 16'bz;  // Controlled_Buffer controlled_buffer_1

  // Notes on the sheet:
  //   PIN
endmodule

module inputSum (
  input  in_1,
  input  in_2,
  input  in_3,
  input  confirm,
  input  enable,
  input  clock,
  input  next,
  output [15:0] out_8,
  output [15:0] out_9
);

  wire and_1_out, counter_1_carry, not_1_out, not_2_out;
  wire [2:0] counter_5_q;
  wire [5:0] counter_1_q;
  wire [15:0] adder_1_out, adder_2_out, counter_2_q, counter_3_q, counter_4_q, multiplexer_1_out,
       multiplier_1_out, multiplier_2_out, multiplier_3_out;

  Counter #(.width(6), .max('h32)) counter_1 (
    .count(clock), .Q(counter_1_q), .carry(counter_1_carry), .clk(clock), .clr(not_1_out));  // open: load, D
  not not_1 (not_1_out, enable);
  not not_2 (not_2_out, enable);
  and and_1 (and_1_out, enable, counter_1_carry);
  Counter #(.width(16), .max('h1)) counter_2 (
    .count(in_3), .Q(counter_2_q), .clk(and_1_out), .clr(not_2_out));  // open: load, D, carry
  Counter #(.width(16), .max('h9)) counter_3 (
    .count(in_2), .Q(counter_3_q), .clk(and_1_out), .clr(not_2_out));  // open: load, D, carry
  Counter #(.width(16), .max('h9)) counter_4 (
    .count(in_1), .Q(counter_4_q), .clk(and_1_out), .clr(not_2_out));  // open: load, D, carry
  Multiplier #(.width(16)) multiplier_1 (.a(counter_2_q), .b(16'h5), .out(multiplier_1_out));  // open: cin, cout
  Multiplier #(.width(16)) multiplier_2 (.a(counter_3_q), .b(16'ha), .out(multiplier_2_out));  // open: cin, cout
  Multiplier #(.width(16)) multiplier_3 (.a(counter_4_q), .b(16'h64), .out(multiplier_3_out));  // open: cin, cout
  Adder #(.width(16)) adder_1 (.a(multiplier_2_out), .b(multiplier_3_out), .out(adder_1_out));  // open: cin, cout
  Counter #(.width(3), .max('h5)) counter_5 (
    .count(next), .Q(counter_5_q), .clk(next), .clr(not_2_out));  // open: load, D, carry
  Multiplexer #(.select(3), .width(16), .enable("false")) multiplexer_1 (
    .in0(16'ha), .in1(16'h32), .in2(16'h64), .in3(16'hc8), .in4(16'h1f4), .in5(adder_2_out),
    .out(multiplexer_1_out), .sel(counter_5_q));  // open: in6, in7
  Adder #(.width(16)) adder_2 (.a(multiplier_1_out), .b(adder_1_out), .out(adder_2_out));  // open: cin, cout
  assign out_8 = enable ? multiplexer_1_out : 16'bz;  // Controlled_Buffer controlled_buffer_1
  Register #(.width(16)) register_1 (.D(multiplexer_1_out), .en(1'b1), .Q(out_9), .clk(confirm));  // open: clr

  // Notes on the sheet:
  //   SUM afis
  //   Sum
endmodule

module bancnote (
  input  in_1,
  input  in_2,
  input  in_3,
  input  in_4,
  input  in_5,
  input  in_6,
  input  reset,
  input  in_8,
  input  in_9,
  output [15:0] out_10,
  output [15:0] out_11,
  output [15:0] out_12,
  output [15:0] sumTotal,
  output [15:0] out_14,
  output [15:0] out_15,
  output [15:0] _500
);

  wire and_1_out, counter_1_carry, not_1_out, not_2_out, or_1_out;
  wire [15:0] adder_1_out, adder_2_out, adder_3_out, adder_4_out, multiplier_1_out, multiplier_2_out,
       multiplier_3_out, multiplier_4_out, multiplier_5_out, multiplier_6_out;

  Counter #(.width(6), .max('h32)) counter_1 (
    .count(in_9), .carry(counter_1_carry), .clk(in_9), .clr(not_1_out));  // open: load, D, Q
  not not_1 (not_1_out, in_8);
  not not_2 (not_2_out, in_8);
  or or_1 (or_1_out, reset, not_2_out);
  and and_1 (and_1_out, in_8, counter_1_carry);
  Counter #(.width(16), .max('h32)) counter_2 (
    .count(in_6), .Q(out_10), .clk(and_1_out), .clr(or_1_out));  // open: load, D, carry
  Counter #(.width(16), .max('h32)) counter_3 (
    .count(in_5), .Q(out_11), .clk(and_1_out), .clr(or_1_out));  // open: load, D, carry
  Counter #(.width(16), .max('h32)) counter_4 (
    .count(in_4), .Q(out_12), .clk(and_1_out), .clr(or_1_out));  // open: load, D, carry
  Counter #(.width(16), .max('h32)) counter_5 (
    .count(in_3), .Q(out_14), .clk(and_1_out), .clr(or_1_out));  // open: load, D, carry
  Counter #(.width(16), .max('h32)) counter_6 (
    .count(in_2), .Q(out_15), .clk(and_1_out), .clr(or_1_out));  // open: load, D, carry
  Counter #(.width(16), .max('h32)) counter_7 (
    .count(in_1), .Q(_500), .clk(and_1_out), .clr(or_1_out));  // open: load, D, carry
  Multiplier #(.width(16)) multiplier_1 (.a(16'h5), .b(out_10), .out(multiplier_1_out));  // open: cin, cout
  Multiplier #(.width(16)) multiplier_2 (.a(16'ha), .b(out_11), .out(multiplier_2_out));  // open: cin, cout
  Multiplier #(.width(16)) multiplier_3 (.a(16'h32), .b(out_12), .out(multiplier_3_out));  // open: cin, cout
  Multiplier #(.width(16)) multiplier_4 (.a(16'h64), .b(out_14), .out(multiplier_4_out));  // open: cin, cout
  Multiplier #(.width(16)) multiplier_5 (.a(16'hc8), .b(out_15), .out(multiplier_5_out));  // open: cin, cout
  Multiplier #(.width(16)) multiplier_6 (.a(16'h1f4), .b(_500), .out(multiplier_6_out));  // open: cin, cout
  Adder #(.width(16)) adder_1 (.a(multiplier_1_out), .b(multiplier_2_out), .out(adder_1_out));  // open: cin, cout
  Adder #(.width(16)) adder_2 (.a(multiplier_3_out), .b(multiplier_4_out), .out(adder_2_out));  // open: cin, cout
  Adder #(.width(16)) adder_3 (.a(multiplier_5_out), .b(multiplier_6_out), .out(adder_3_out));  // open: cin, cout
  Adder #(.width(16)) adder_4 (.a(adder_1_out), .b(adder_2_out), .out(adder_4_out));  // open: cin, cout
  Adder #(.width(16)) adder_5 (.a(adder_4_out), .b(adder_3_out), .out(sumTotal));  // open: cin, cout

  // Notes on the sheet:
  //   enable
endmodule

module depunere (
  input  in_1,
  input  in_2,
  input  in_3,
  input  in_4,
  input  in_5,
  input  in_6,
  input  [15:0] in_7,
  input  in_8,
  input  in_9,
  input  [15:0] in_10,
  input  in_11,
  input  in_12,
  output [15:0] out_13,
  output [15:0] cont_out,
  output store_cont,
  output [3:0] out_16,
  output [15:0] out_17,
  output store_banc,
  output out_19
);

  wire and_1_out, counter_1_carry, counter_3_carry, multiplexer_1_out, not_1_out, not_2_out;
  wire [15:0] bancnote_1__500, bancnote_1_out_10, bancnote_1_out_11, bancnote_1_out_12, bancnote_1_out_14,
       bancnote_1_out_15, multiplexer_2_out;

  Counter #(.ongoal("stay")) counter_1 (
    .carry(counter_1_carry), .clk(in_12), .clr(not_1_out));  // open: load, D, count, Q
  not not_1 (not_1_out, in_8);
  and and_1 (and_1_out, in_8, multiplexer_1_out);
  Multiplexer #(.enable("false")) multiplexer_1 (
    .in0(1'b0), .in1(in_11), .out(multiplexer_1_out), .sel(counter_1_carry));
  D_Flip_Flop d_ff_1 (.clk(in_12), .D(1'b1), .Q(store_banc), .en(and_1_out), .reset(out_19));  // open: Qn, preset
  not not_2 (not_2_out, in_8);
  bancnote bancnote_1 (
    .in_8(in_8), .sumTotal(out_13), .in_1(in_1), .in_2(in_2), .in_3(in_3), .in_4(in_4), .in_5(in_5),
    .in_6(in_6), .out_10(bancnote_1_out_10), .out_11(bancnote_1_out_11), .out_12(bancnote_1_out_12),
    .out_14(bancnote_1_out_14), .out_15(bancnote_1_out_15), ._500(bancnote_1__500), .reset(in_9), .in_9(in_12));
  Counter #(.width(4), .max('h7), .ongoal("stay")) counter_2 (
    .count(store_banc), .Q(out_16), .carry(out_19), .clk(in_12), .clr(not_2_out));  // open: load, D
  Adder #(.width(16)) adder_1 (.a(in_7), .b(out_13), .out(cont_out));  // open: cin, cout
  Multiplexer #(.select(4), .width(16), .enable("false")) multiplexer_2 (
    .in0(bancnote_1__500), .in1(bancnote_1_out_15), .in2(bancnote_1_out_14), .in3(bancnote_1_out_12),
    .in4(bancnote_1_out_11), .in5(bancnote_1_out_10), .in6({16{1'b0}}), .out(multiplexer_2_out), .sel(out_16));  // open: in7, in8, in9, in10, in11, in12, in13, in14, in15
  Counter #(.width(2), .max('h2), .ongoal("stay")) counter_3 (
    .count(out_19), .carry(counter_3_carry), .clk(in_12), .clr(not_2_out));  // open: load, D, Q
  Adder #(.width(16)) adder_2 (.a(in_10), .b(multiplexer_2_out), .out(out_17));  // open: cin, cout
  T_Flip_Flop t_ff_1 (.clk(in_12), .T(out_19), .Q(store_cont), .reset(counter_3_carry));  // open: Qn, preset, en

  // Notes on the sheet:
  //   sum depusa
  //   banc in
  //   adressbanc out
  //   banc out
  //   cont in
  //   depunere finish
endmodule

module retragereBanc (
  input  [15:0] in_1,
  input  in_2,
  input  in_3,
  input  [15:0] in_4,
  input  in_5,
  output out_6,
  output [3:0] out_7,
  output [15:0] Numar_bancnote,
  output [15:0] out_9,
  output out_10,
  output [3:0] out_11
);

  wire and_1_out, and_2_out, and_3_out, and_4_out, and_5_out, and_6_out, and_8_out, and_9_out,
       comparator_1_eq, comparator_2_eq, comparator_2_lt, comparator_3_lt, comparator_4_eq, counter_1_q,
       counter_2_carry, counter_3_carry, counter_3_q, counter_4_carry, counter_5_q, not_1_out, not_2_out,
       or_1_out, or_2_out;
  wire [3:0] counter_2_q, counter_6_q, multiplexer_3_out, multiplexer_7_out;
  wire [15:0] divider_1_out, divider_1_rem, multiplexer_4_out, multiplexer_5_out, multiplexer_6_out,
       multiplexer_9_out, multiplier_1_out, ram_1_data, register_1_q, rom_1_data, subtractor_1_out,
       subtractor_2_out;

  Multiplexer #(.width(16), .enable("false")) multiplexer_1 (
    .in0(in_4), .in1(ram_1_data), .out(out_9), .sel(and_1_out));
  Multiplexer #(.width(4), .enable("false")) multiplexer_2 (
    .in0(counter_2_q), .in1(counter_6_q), .out(out_11), .sel(and_1_out));
  and and_1 (and_1_out, and_8_out, in_5);
  and and_2 (and_2_out, in_2, in_3);
  Counter #(.width(1), .max('h1), .ongoal("stay")) counter_1 (
    .count(counter_4_carry), .Q(counter_1_q), .clk(counter_4_carry), .clr(not_1_out));  // open: load, D, carry
  not not_1 (not_1_out, in_2);
  or or_1 (or_1_out, comparator_4_eq, comparator_3_lt);
  Multiplexer #(.width(4), .enable("false")) multiplexer_3 (
    .in0(counter_2_q), .in1(out_7), .out(multiplexer_3_out), .sel(counter_2_carry));
  Multiplexer #(.width(16), .enable("false")) multiplexer_4 (
    .in0(in_4), .in1(subtractor_1_out), .out(multiplexer_4_out), .sel(counter_2_carry));
  Counter #(.width(4), .max('h6), .ongoal("stay")) counter_2 (
    .count(and_2_out), .Q(counter_2_q), .carry(counter_2_carry), .clk(and_2_out), .clr(not_1_out));  // open: load, D
  and and_3 (and_3_out, counter_2_carry, and_2_out);
  and and_4 (and_4_out, or_1_out, counter_3_carry);
  and and_5 (and_5_out, and_3_out, ~counter_1_q);  // AND_Gate
  Counter #(.width(1), .max('h1), .ongoal("stay")) counter_3 (
    .count(and_5_out), .Q(counter_3_q), .carry(counter_3_carry), .clk(and_5_out), .clr(counter_4_carry));  // open: load, D
  Register #(.width(16)) register_1 (
    .D(multiplexer_5_out), .en(and_5_out), .Q(register_1_q), .clk(and_5_out));  // open: clr
  Multiplexer #(.width(16), .enable("false")) multiplexer_5 (
    .in0(in_1), .in1(multiplexer_9_out), .out(multiplexer_5_out), .sel(counter_3_q));
  ROM #(.addrWidth(4), .dataWidth(16)) rom_1 (.addr(out_7), .data(rom_1_data), .sel(1'b1));
  Counter #(.width(4), .max('h6)) counter_4 (
    .count(and_4_out), .Q(out_7), .carry(counter_4_carry), .clk(and_5_out), .clr(counter_4_carry));  // open: load, D
  Comparator #(.width(16), .mode("unsigned")) comparator_1 (
    .a(register_1_q), .b({16{1'b0}}), .eq(comparator_1_eq));  // open: gt, lt
  Comparator #(.width(16), .mode("unsigned")) comparator_2 (
    .a(ram_1_data), .b(divider_1_out), .eq(comparator_2_eq), .lt(comparator_2_lt));  // open: gt
  or or_2 (or_2_out, comparator_2_eq, comparator_2_lt);
  not not_2 (not_2_out, comparator_1_eq);
  Comparator #(.width(16), .mode("unsigned")) comparator_3 (
    .a(register_1_q), .b(rom_1_data), .lt(comparator_3_lt));  // open: gt, eq
  Multiplexer #(.width(16), .enable("false")) multiplexer_6 (
    .in0(divider_1_out), .in1(ram_1_data), .out(multiplexer_6_out), .sel(or_2_out));
  and and_6 (and_6_out, counter_1_q, comparator_1_eq);
  and and_7 (out_6, counter_1_q, not_2_out);
  Subtractor #(.width(16)) subtractor_1 (
    .a(ram_1_data), .b(multiplexer_6_out), .out(subtractor_1_out));  // open: bin, bout
  Multiplexer #(.width(4), .enable("false")) multiplexer_7 (
    .in0(multiplexer_3_out), .in1(counter_6_q), .out(multiplexer_7_out), .sel(and_8_out));
  Divider #(.width(16)) divider_1 (
    .a(register_1_q), .b(rom_1_data), .out(divider_1_out), .rem(divider_1_rem));  // open: upper
  RAM #(.addrWidth(4), .dataWidth(16), .bus("separate")) ram_1 (
    .addr(multiplexer_7_out), .din(multiplexer_4_out), .data(ram_1_data), .str(1'b1), .sel(1'b1),
    .clk(and_2_out), .ld(1'b1));  // open: clr
  Multiplexer #(.width(16), .disabled(0), .enable("false")) multiplexer_8 (
    .in0(divider_1_out), .in1(ram_1_data), .out(Numar_bancnote), .sel(comparator_2_lt));
  Comparator #(.width(16), .mode("unsigned")) comparator_4 (
    .a(ram_1_data), .b({16{1'b0}}), .eq(comparator_4_eq));  // open: gt, lt
  Multiplier #(.width(16)) multiplier_1 (.a(rom_1_data), .b(ram_1_data), .out(multiplier_1_out));  // open: cin, cout
  and and_8 (and_8_out, counter_1_q, and_6_out);
  Subtractor #(.width(16)) subtractor_2 (
    .a(register_1_q), .b(multiplier_1_out), .out(subtractor_2_out));  // open: bin, bout
  Counter #(.width(1), .max('h1), .ongoal("stay")) counter_5 (
    .count(and_9_out), .Q(counter_5_q), .clk(and_9_out), .clr(not_1_out));  // open: load, D, carry
  and and_9 (and_9_out, and_8_out, and_2_out);
  Counter #(.width(4), .max('h6), .ongoal("stay")) counter_6 (
    .count(counter_5_q), .Q(counter_6_q), .carry(out_10), .clk(and_9_out), .clr(not_1_out));  // open: load, D
  Multiplexer #(.width(16), .disabled(0), .enable("false")) multiplexer_9 (
    .in0(divider_1_rem), .in1(subtractor_2_out), .out(multiplexer_9_out), .sel(comparator_2_lt));

  // Notes on the sheet:
  //   contents of rom_1 (hex, n*v repeats v):
  //   1f4 c8 64 32 a 5
  //   val bancnota
endmodule

module afisor (
  input  [31:0] in_1,
  input  in_2,
  input  in_3,
  input  in_4,
  input  in_5,
  input  in_6,
  output [6:0] out_7,
  output [7:0] out_8
);

  wire and_1_out, or_1_out;
  wire [2:0] counter_1_q, counter_2_q, multiplexer_6_out;
  wire [3:0] hex_1_out_2, hex_1_out_3, hex_1_out_4, hex_1_out_5, hex_1_out_6, hex_1_out_7, hex_1_out_8,
       hex_1_out_9, multiplexer_1_out, multiplexer_2_out, multiplexer_3_out, multiplexer_4_out,
       multiplexer_5_out;
  wire [7:0] decoder_1_out0;

  Multiplexer #(.select(3), .width(4), .enable("false")) multiplexer_1 (
    .in0(4'b0000), .in1(4'b1010), .in2(4'b1100), .in3(4'b1100), .in4(4'b0000), .in5(4'b0000), .in6(4'b0000),
    .in7(4'b0000), .out(multiplexer_1_out), .sel(multiplexer_6_out));
  Multiplexer #(.select(3), .width(4), .enable("false")) multiplexer_2 (
    .in0(4'b0000), .in1(4'b1010), .in2(4'b1010), .in3(4'b1100), .in4(4'b0000), .in5(4'b0000), .in6(4'b0000),
    .in7(4'b0000), .out(multiplexer_2_out), .sel(multiplexer_6_out));
  and and_1 (and_1_out, in_2, in_3);
  hex hex_1 (
    .in_1(in_1), .out_2(hex_1_out_2), .out_3(hex_1_out_3), .out_4(hex_1_out_4), .out_5(hex_1_out_5),
    .out_6(hex_1_out_6), .out_7(hex_1_out_7), .out_8(hex_1_out_8), .out_9(hex_1_out_9));
  Multiplexer #(.width(4), .enable("false")) multiplexer_3 (
    .in0(multiplexer_1_out), .in1(multiplexer_2_out), .out(multiplexer_3_out), .sel(in_6));
  Multiplexer #(.select(3), .width(4), .enable("false")) multiplexer_4 (
    .in0(hex_1_out_2), .in1(hex_1_out_3), .in2(hex_1_out_4), .in3(hex_1_out_5), .in4(hex_1_out_6),
    .in5(hex_1_out_7), .in6(hex_1_out_8), .in7(hex_1_out_9), .out(multiplexer_4_out), .sel(multiplexer_6_out));
  Counter #(.width(3), .max('h7)) counter_1 (.Q(counter_1_q), .clk(and_1_out));  // open: load, D, count, carry, clr
  Counter #(.width(3), .max('h3)) counter_2 (.Q(counter_2_q), .clk(and_1_out));  // open: load, D, count, carry, clr
  Multiplexer #(.width(4), .enable("false")) multiplexer_5 (
    .in0(multiplexer_4_out), .in1(multiplexer_3_out), .out(multiplexer_5_out), .sel(or_1_out));
  or or_1 (or_1_out, in_6, in_5);
  Multiplexer #(.width(3), .enable("false")) multiplexer_6 (
    .in0(counter_2_q), .in1(counter_1_q), .out(multiplexer_6_out), .sel(in_4));
  decod_Afis decod_afis_1 (
    .bit4(multiplexer_5_out[3]), .bit3(multiplexer_5_out[2]), .bit2(multiplexer_5_out[1]),
    .bit1(multiplexer_5_out[0]), .a(out_7[0]), .b(out_7[1]), .c(out_7[2]), .d(out_7[3]), .e(out_7[4]),
    .f(out_7[5]), .g(out_7[6]));
  Decoder #(.select(3), .enable("false")) decoder_1 (
    .out0(decoder_1_out0[0]), .out1(decoder_1_out0[1]), .out2(decoder_1_out0[2]), .out3(decoder_1_out0[3]),
    .out4(decoder_1_out0[4]), .out5(decoder_1_out0[5]), .out6(decoder_1_out0[6]), .out7(decoder_1_out0[7]),
    .sel(multiplexer_6_out));
  Multiplexer #(.width(8), .enable("false")) multiplexer_7 (
    .in0({8{1'b0}}), .in1(decoder_1_out0), .out(out_8), .sel(in_2));
endmodule

module enable_afisor (
  input  [6:0] in_1,
  input  in_2,
  output [6:0] out_3
);

  wire [6:0] undriven, undriven_2, undriven_3, undriven_4, undriven_5, undriven_6, undriven_7, undriven_8;

  _7_Segment_Display u_7_segment_display_1 (
    .g(undriven[6]), .f(undriven[5]), .a(undriven[0]), .b(undriven[1]), .e(undriven[4]), .d(undriven[3]),
    .c(undriven[2]));  // open: dp
  and and_1 (out_3[0], in_1[0], in_2);
  and and_2 (out_3[1], in_1[1], in_2);
  and and_3 (out_3[2], in_1[2], in_2);
  and and_4 (out_3[3], in_1[3], in_2);
  and and_5 (out_3[4], in_1[4], in_2);
  and and_6 (out_3[5], in_1[5], in_2);
  and and_7 (out_3[6], in_1[6], in_2);
  _7_Segment_Display u_7_segment_display_2 (
    .g(undriven_2[6]), .f(undriven_2[5]), .a(undriven_2[0]), .b(undriven_2[1]), .e(undriven_2[4]),
    .d(undriven_2[3]), .c(undriven_2[2]));  // open: dp
  _7_Segment_Display u_7_segment_display_3 (
    .g(undriven_3[6]), .f(undriven_3[5]), .a(undriven_3[0]), .b(undriven_3[1]), .e(undriven_3[4]),
    .d(undriven_3[3]), .c(undriven_3[2]));  // open: dp
  _7_Segment_Display u_7_segment_display_4 (
    .g(undriven_4[6]), .f(undriven_4[5]), .a(undriven_4[0]), .b(undriven_4[1]), .e(undriven_4[4]),
    .d(undriven_4[3]), .c(undriven_4[2]));  // open: dp
  _7_Segment_Display u_7_segment_display_5 (
    .g(undriven_5[6]), .f(undriven_5[5]), .a(undriven_5[0]), .b(undriven_5[1]), .e(undriven_5[4]),
    .d(undriven_5[3]), .c(undriven_5[2]));  // open: dp
  _7_Segment_Display u_7_segment_display_6 (
    .g(undriven_6[6]), .f(undriven_6[5]), .a(undriven_6[0]), .b(undriven_6[1]), .e(undriven_6[4]),
    .d(undriven_6[3]), .c(undriven_6[2]));  // open: dp
  _7_Segment_Display u_7_segment_display_7 (
    .g(undriven_7[6]), .f(undriven_7[5]), .a(undriven_7[0]), .b(undriven_7[1]), .e(undriven_7[4]),
    .d(undriven_7[3]), .c(undriven_7[2]));  // open: dp
  _7_Segment_Display u_7_segment_display_8 (
    .g(undriven_8[6]), .f(undriven_8[5]), .a(undriven_8[0]), .b(undriven_8[1]), .e(undriven_8[4]),
    .d(undriven_8[3]), .c(undriven_8[2]));  // open: dp
endmodule

module decod_Afis (
  input  bit4,
  input  bit3,
  input  bit2,
  input  bit1,
  output a,
  output b,
  output c,
  output d,
  output e,
  output f,
  output g
);

  wire and_1_out, and_2_out, and_3_out, and_4_out, and_5_out, and_6_out, and_7_out, and_8_out, and_9_out,
       and_10_out, and_11_out, and_12_out, and_13_out, and_14_out, and_15_out, and_16_out, and_17_out,
       and_18_out, and_19_out, and_20_out, and_21_out, and_22_out, and_23_out, not_1_out, not_2_out,
       not_3_out, not_4_out, not_5_out, not_6_out, not_7_out, not_8_out, not_9_out, not_10_out, not_11_out,
       not_12_out, not_13_out, not_14_out, not_15_out, not_16_out, not_17_out, not_18_out, not_19_out,
       not_20_out, not_21_out, not_22_out, not_23_out, not_24_out, not_25_out, not_26_out, not_27_out,
       not_28_out, not_29_out, not_30_out, not_31_out, not_32_out, not_33_out, not_34_out, not_35_out,
       not_36_out, not_37_out;

  not not_1 (not_1_out, bit3);
  and and_1 (and_1_out, not_1_out, not_2_out);
  not not_2 (not_2_out, bit1);
  and and_2 (and_2_out, bit3, bit1);
  and and_3 (and_3_out, bit4, not_3_out);
  not not_3 (not_3_out, bit3);
  not not_4 (not_4_out, bit4);
  and and_4 (and_4_out, not_4_out, not_5_out, not_6_out);
  not not_5 (not_5_out, bit2);
  not not_6 (not_6_out, bit1);
  not not_7 (not_7_out, bit3);
  and and_5 (and_5_out, bit2, bit1);
  not not_8 (not_8_out, bit4);
  and and_6 (and_6_out, not_8_out, not_9_out);
  not not_9 (not_9_out, bit2);
  not not_10 (not_10_out, bit4);
  and and_7 (and_7_out, not_10_out, bit3);
  and and_8 (and_8_out, bit4, not_11_out);
  not not_11 (not_11_out, bit3);
  not not_12 (not_12_out, bit4);
  not not_13 (not_13_out, bit3);
  and and_9 (and_9_out, not_12_out, not_13_out, not_14_out);
  not not_14 (not_14_out, bit1);
  not not_15 (not_15_out, bit4);
  not not_16 (not_16_out, bit3);
  and and_10 (and_10_out, not_15_out, not_16_out, bit2);
  not not_17 (not_17_out, bit4);
  and and_11 (and_11_out, not_17_out, bit2, not_18_out);
  not not_18 (not_18_out, bit1);
  and and_12 (and_12_out, bit3, not_19_out, bit1);
  not not_19 (not_19_out, bit2);
  and and_13 (and_13_out, bit4, not_20_out, not_21_out);
  not not_20 (not_20_out, bit3);
  not not_21 (not_21_out, bit2);
  not not_22 (not_22_out, bit3);
  and and_14 (and_14_out, not_22_out, not_23_out);
  not not_23 (not_23_out, bit1);
  and and_15 (and_15_out, bit2, not_24_out);
  not not_24 (not_24_out, bit1);
  not not_25 (not_25_out, bit4);
  not not_26 (not_26_out, bit2);
  and and_16 (and_16_out, not_25_out, not_26_out, not_27_out);
  not not_27 (not_27_out, bit1);
  not not_28 (not_28_out, bit4);
  and and_17 (and_17_out, not_28_out, bit3, not_29_out);
  not not_29 (not_29_out, bit2);
  not not_30 (not_30_out, bit4);
  and and_18 (and_18_out, not_30_out, bit3, not_31_out);
  not not_31 (not_31_out, bit1);
  and and_19 (and_19_out, bit4, not_32_out);
  not not_32 (not_32_out, bit3);
  not not_33 (not_33_out, bit3);
  and and_20 (and_20_out, not_33_out, bit2);
  and and_21 (and_21_out, bit2, not_34_out);
  not not_34 (not_34_out, bit1);
  not not_35 (not_35_out, bit4);
  and and_22 (and_22_out, not_35_out, bit3, not_36_out);
  not not_36 (not_36_out, bit2);
  and and_23 (and_23_out, bit4, not_37_out);
  not not_37 (not_37_out, bit3);
  or or_1 (a, and_1_out, bit2, and_2_out, and_3_out);
  or or_2 (b, and_4_out, not_7_out, and_5_out);
  or or_3 (c, and_6_out, bit1, and_7_out, and_8_out);
  or or_4 (d, and_9_out, and_10_out, and_11_out, and_12_out, and_13_out);
  or or_5 (e, and_14_out, and_15_out);
  or or_6 (f, and_16_out, and_17_out, and_18_out, and_19_out);
  or or_7 (g, and_20_out, and_21_out, and_22_out, and_23_out);
endmodule

module hex (
  input  [31:0] in_1,
  output [3:0] out_2,
  output [3:0] out_3,
  output [3:0] out_4,
  output [3:0] out_5,
  output [3:0] out_6,
  output [3:0] out_7,
  output [3:0] out_8,
  output [3:0] out_9
);

  wire [31:0] divider_1_out, divider_2_out, divider_3_out, divider_4_out, divider_5_out, divider_6_out,
       divider_7_out;
  wire [31:4] divider_1_rem, divider_2_rem, divider_3_rem, divider_4_rem, divider_5_rem, divider_6_rem,
       divider_7_rem, divider_8_rem;

  Divider #(.width(32)) divider_1 (
    .a(in_1), .b(32'ha), .out(divider_1_out), .rem({divider_1_rem, out_2}));  // open: upper
  Divider #(.width(32)) divider_2 (
    .a(divider_1_out), .b(32'ha), .out(divider_2_out), .rem({divider_2_rem, out_3}));  // open: upper
  Divider #(.width(32)) divider_3 (
    .a(divider_2_out), .b(32'ha), .out(divider_3_out), .rem({divider_3_rem, out_4}));  // open: upper
  Divider #(.width(32)) divider_4 (
    .a(divider_3_out), .b(32'ha), .out(divider_4_out), .rem({divider_4_rem, out_5}));  // open: upper
  Divider #(.width(32)) divider_5 (
    .a(divider_4_out), .b(32'ha), .out(divider_5_out), .rem({divider_5_rem, out_6}));  // open: upper
  Divider #(.width(32)) divider_6 (
    .a(divider_5_out), .b(32'ha), .out(divider_6_out), .rem({divider_6_rem, out_7}));  // open: upper
  Divider #(.width(32)) divider_7 (
    .a(divider_6_out), .b(32'ha), .out(divider_7_out), .rem({divider_7_rem, out_8}));  // open: upper
  Divider #(.width(32)) divider_8 (.a(divider_7_out), .b(32'ha), .rem({divider_8_rem, out_9}));  // open: out, upper
endmodule

module retragere_cont (
  input  [15:0] in_1,
  input  [15:0] in_2,
  input  in_3,
  input  in_4,
  output [15:0] out_5,
  output out_6,
  output out_7
);

  wire comparator_1_lt, counter_1_carry, not_1_out, not_2_out, t_ff_1_q;
  wire [15:0] register_1_q, subtractor_1_out;

  not not_1 (not_1_out, in_3);
  Counter #(.width(1), .max('h1), .ongoal("stay")) counter_1 (
    .count(in_4), .carry(counter_1_carry), .clk(in_4), .clr(not_1_out));  // open: load, D, Q
  Subtractor #(.width(16)) subtractor_1 (.a(register_1_q), .b(in_1), .out(subtractor_1_out));  // open: bin, bout
  not not_2 (not_2_out, counter_1_carry);
  T_Flip_Flop t_ff_1 (.clk(in_4), .T(not_2_out), .Q(t_ff_1_q), .reset(not_1_out), .en(in_4));  // open: Qn, preset
  Multiplexer #(.width(16), .enable("false")) multiplexer_1 (
    .in0(subtractor_1_out), .in1(register_1_q), .out(out_5), .sel(comparator_1_lt));
  and and_1 (out_6, t_ff_1_q, comparator_1_lt);
  and and_2 (out_7, t_ff_1_q, ~comparator_1_lt);  // AND_Gate
  Comparator #(.width(16), .mode("unsigned")) comparator_1 (
    .a(register_1_q), .b(in_1), .lt(comparator_1_lt));  // open: gt, eq
  Register #(.width(16)) register_1 (
    .D(in_2), .en(counter_1_carry), .Q(register_1_q), .clk(counter_1_carry), .clr(not_1_out));
endmodule

module retragere (
  input  [15:0] in_1,
  input  [15:0] in_2,
  input  in_3,
  input  in_4,
  input  [15:0] in_5,
  output [31:0] out_6,
  output [15:0] out_7,
  output out_8,
  output out_9,
  output [3:0] out_10,
  output [15:0] out_11
);

  wire and_1_out, and_2_out, comparator_1_gt, counter_1_q, counter_2_carry, not_1_out,
       retragere_cont_1_out_6, retragere_cont_1_out_7, retragerebanc_1_out_6, retragerebanc_1_out_10;
  wire [3:0] counter_3_q, multiplexer_3_out, retragerebanc_1_out_7;
  wire [15:0] ram_1_data, retragere_cont_1_out_5, retragerebanc_1_numar_bancnote, rom_1_data;
  wire [31:0] adder_1_out, bit_extender_1_out, bit_extender_2_out, multiplier_1_out;

  Counter #(.width(1), .max('h1), .ongoal("stay")) counter_1 (
    .count(in_4), .Q(counter_1_q), .clk(in_4), .clr(not_1_out));  // open: load, D, carry
  not not_1 (not_1_out, in_3);
  and and_1 (and_1_out, in_4, counter_1_q);
  retragere_cont retragere_cont_1 (
    .in_1(in_1), .in_2(in_2), .in_3(in_3), .out_5(retragere_cont_1_out_5), .out_6(retragere_cont_1_out_6),
    .out_7(retragere_cont_1_out_7), .in_4(and_1_out));
  Multiplexer #(.width(16), .enable("false")) multiplexer_1 (
    .in0(in_2), .in1(retragere_cont_1_out_5), .out(out_7), .sel(retragerebanc_1_out_10));
  Counter #(.width(7), .max('h7f)) counter_2 (
    .count(and_2_out), .carry(counter_2_carry), .clk(and_1_out), .clr(not_1_out));  // open: load, D, Q
  retragereBanc retragerebanc_1 (
    .in_1(in_1), .in_2(in_3), .in_3(and_1_out), .in_4(in_5), .out_6(retragerebanc_1_out_6),
    .Numar_bancnote(retragerebanc_1_numar_bancnote), .out_9(out_11), .out_10(retragerebanc_1_out_10),
    .out_11(out_10), .out_7(retragerebanc_1_out_7), .in_5(retragere_cont_1_out_7));
  and and_2 (and_2_out, retragere_cont_1_out_7, retragerebanc_1_out_10);
  or or_1 (out_8, retragere_cont_1_out_6, retragerebanc_1_out_6);
  Counter #(.width(4), .max('h5), .ongoal("stay")) counter_3 (
    .count(and_2_out), .Q(counter_3_q), .carry(out_9), .clk(counter_2_carry), .clr(not_1_out));  // open: load, D
  Comparator #(.width(16), .mode("unsigned")) comparator_1 (
    .a(retragerebanc_1_numar_bancnote), .b({16{1'b0}}), .gt(comparator_1_gt));  // open: eq, lt
  Multiplexer #(.width(32), .enable("false")) multiplexer_2 (
    .in0({32{1'b0}}), .in1(adder_1_out), .out(out_6), .sel(and_2_out));
  Multiplexer #(.width(4), .enable("false")) multiplexer_3 (
    .in0(retragerebanc_1_out_7), .in1(counter_3_q), .out(multiplexer_3_out), .sel(and_2_out));
  assign bit_extender_1_out = {{16{1'b0}}, ram_1_data};  // Bit_Extender bit_extender_1
  RAM #(.addrWidth(4), .dataWidth(16), .bus("separate")) ram_1 (
    .addr(multiplexer_3_out), .din(retragerebanc_1_numar_bancnote), .data(ram_1_data), .str(comparator_1_gt),
    .sel(1'b1), .clk(and_1_out), .ld(1'b1), .clr(not_1_out));
  ROM #(.addrWidth(4), .dataWidth(16)) rom_1 (.addr(counter_3_q), .data(rom_1_data));  // open: sel
  assign bit_extender_2_out = {{16{1'b0}}, rom_1_data};  // Bit_Extender bit_extender_2
  Multiplier #(.width(32)) multiplier_1 (
    .a(32'h2710), .b(bit_extender_1_out), .out(multiplier_1_out));  // open: cin, cout
  Adder #(.width(32)) adder_1 (.a(bit_extender_2_out), .b(multiplier_1_out), .out(adder_1_out));  // open: cin, cout

  // Notes on the sheet:
  //   contents of rom_1 (hex, n*v repeats v):
  //   1f4 c8 64 32 a 5
endmodule

module transfer (
  input  [3:0] PIN,
  input  [15:0] in_2,
  input  Confim,
  input  [15:0] Suma,
  input  Enable,
  input  in_6,
  output [3:0] out_7,
  output [15:0] out_8,
  output Failed,
  output Finished,
  output out_11
);

  wire and_1_out, and_2_out, and_3_out, and_4_out, comparator_1_lt, counter_1_carry, counter_2_carry,
       counter_3_carry, counter_4_carry, d_ff_1_q, d_ff_3_q, multiplexer_2_out, multiplexer_3_out, not_1_out,
       not_2_out, not_3_out, not_4_out, not_5_out, or_1_out, subtractor_1_bout;
  wire [1:0] multiplexer_6_out;
  wire [3:0] register_1_q, register_2_q;
  wire [15:0] adder_1_out, multiplexer_5_out, register_3_q, subtractor_1_out;

  and and_1 (and_1_out, Enable, in_6);
  Counter #(.width(2), .max('h3), .ongoal("stay")) counter_1 (
    .count(Enable), .carry(counter_1_carry), .clk(and_1_out));  // open: load, D, Q, clr
  Counter #(.width(2), .max('h2), .ongoal("stay")) counter_2 (
    .count(counter_1_carry), .carry(counter_2_carry), .clk(and_1_out));  // open: load, D, Q, clr
  not not_1 (not_1_out, counter_1_carry);
  and and_2 (and_2_out, ~multiplexer_6_out[0], multiplexer_6_out[1]);  // AND_Gate
  or or_1 (or_1_out, and_2_out, and_3_out);
  Counter #(.width(2), .max('h2), .ongoal("stay")) counter_3 (
    .count(Confim), .carry(counter_3_carry), .clk(Confim), .clr(not_2_out));  // open: load, D, Q
  not not_2 (not_2_out, Enable);
  not not_3 (not_3_out, counter_2_carry);
  Register #(.width(4)) register_1 (.D(PIN), .en(not_1_out), .Q(register_1_q), .clk(and_1_out));  // open: clr
  Register #(.width(4)) register_2 (.D(PIN), .en(and_1_out), .Q(register_2_q), .clk(and_1_out), .clr(not_2_out));
  and and_3 (and_3_out, multiplexer_6_out[1], multiplexer_6_out[0]);
  D_Flip_Flop d_ff_1 (
    .clk(and_1_out), .D(or_1_out), .Q(d_ff_1_q), .en(and_1_out), .reset(not_2_out));  // open: Qn, preset
  Counter #(.width(2), .max('h2), .ongoal("stay")) counter_4 (
    .count(counter_3_carry), .carry(counter_4_carry), .clk(in_6), .clr(not_2_out));  // open: load, D, Q
  Register #(.width(16)) register_3 (.D(in_2), .en(not_3_out), .Q(register_3_q), .clk(and_1_out), .clr(not_2_out));
  Multiplexer #(.width(4), .enable("false")) multiplexer_1 (
    .in0(register_1_q), .in1(register_2_q), .out(out_7), .sel(and_4_out));
  and and_4 (and_4_out, multiplexer_6_out[1], out_11);
  not not_4 (not_4_out, d_ff_1_q);
  D_Flip_Flop d_ff_2 (
    .clk(and_1_out), .D(counter_3_carry), .Q(multiplexer_6_out[1]), .en(and_1_out), .reset(not_2_out));  // open: Qn, preset
  Multiplexer #(.enable("false")) multiplexer_2 (
    .in0(1'b0), .in1(counter_3_carry), .out(multiplexer_2_out), .sel(not_4_out));
  and and_5 (out_11, counter_3_carry, ~counter_4_carry);  // AND_Gate
  Comparator #(.width(16), .mode("unsigned")) comparator_1 (
    .a(register_3_q), .b(Suma), .lt(comparator_1_lt));  // open: gt, eq
  Multiplexer #(.enable("false")) multiplexer_3 (
    .in0(1'b0), .in1(and_1_out), .out(multiplexer_3_out), .sel(multiplexer_2_out));
  Multiplexer #(.select(2), .width(16), .enable("false")) multiplexer_4 (
    .in0(subtractor_1_out), .in1(in_2), .in2(adder_1_out), .in3(in_2), .out(out_8), .sel(multiplexer_6_out));
  Multiplexer #(.width(16), .enable("false")) multiplexer_5 (
    .in0({16{1'b0}}), .in1(Suma), .out(multiplexer_5_out), .sel(multiplexer_2_out));
  Subtractor #(.width(16)) subtractor_1 (
    .a(in_2), .b(multiplexer_5_out), .out(subtractor_1_out), .bout(subtractor_1_bout));  // open: bin
  Adder #(.width(16)) adder_1 (.a(in_2), .b(Suma), .out(adder_1_out));  // open: cin, cout
  D_Flip_Flop d_ff_3 (
    .clk(multiplexer_3_out), .D(subtractor_1_bout), .Q(d_ff_3_q), .en(multiplexer_3_out), .reset(not_2_out));  // open: Qn, preset
  Multiplexer #(.enable("false")) multiplexer_6 (
    .in0(subtractor_1_bout), .in1(d_ff_3_q), .out(multiplexer_6_out[0]), .sel(multiplexer_6_out[1]));
  not not_5 (not_5_out, comparator_1_lt);
  and and_6 (Failed, comparator_1_lt, d_ff_1_q);
  and and_7 (Finished, not_5_out, d_ff_1_q);
endmodule

module pin_cod (
  input  [3:0] in_1,
  output [15:0] out_2
);

  wire [15:0] adder_1_out, adder_2_out;

  Adder #(.width(16)) adder_1 (
    .a({{15{1'b0}}, in_1[0]}), .b({{12{1'b0}}, in_1[1], 1'b0, in_1[1], 1'b0}), .out(adder_1_out));  // open: cin, cout
  Adder #(.width(16)) adder_2 (
    .a({{9{1'b0}}, {2{in_1[2]}}, 2'b00, in_1[2], 2'b00}),
    .b({{6{1'b0}}, {5{in_1[3]}}, 1'b0, in_1[3], 3'b000}), .out(adder_2_out));  // open: cin, cout
  Adder #(.width(16)) adder_3 (.a(adder_1_out), .b(adder_2_out), .out(out_2));  // open: cin, cout
endmodule

module selectie_afisor (
  input  [15:0] in_1,
  input  in_2,
  input  [15:0] in_3,
  input  in_4,
  input  [15:0] in_5,
  input  in_6,
  input  [31:0] in_7,
  input  in_8,
  input  in_9,
  input  in_10,
  input  [15:0] in_11,
  input  in_12,
  input  in_13,
  output [31:0] out_14
);

  wire and_1_out, and_2_out, counter_1_q, not_1_out;
  wire [15:0] controlled_buffer_1_out, multiplexer_1_out, register_1_q;
  wire [31:0] bit_extender_1_out;

  Register #(.width(16)) register_1 (.D(in_3), .en(in_4), .Q(register_1_q), .clk(in_10), .clr(not_1_out));
  Multiplexer #(.width(16), .enable("false")) multiplexer_1 (
    .in0(in_1), .in1(register_1_q), .out(multiplexer_1_out), .sel(counter_1_q));
  Counter #(.width(1), .max('h1), .ongoal("stay")) counter_1 (
    .count(in_13), .Q(counter_1_q), .clk(in_13), .clr(not_1_out));  // open: load, D, carry
  assign controlled_buffer_1_out = in_12 ? in_11 : 16'bz;  // Controlled_Buffer controlled_buffer_1
  assign controlled_buffer_1_out = and_1_out ? in_1 : 16'bz;  // Controlled_Buffer controlled_buffer_2
  and and_1 (and_1_out, in_2, ~in_9);  // AND_Gate
  assign controlled_buffer_1_out = and_2_out ? in_3 : 16'bz;  // Controlled_Buffer controlled_buffer_3
  and and_2 (and_2_out, in_4, ~in_9);  // AND_Gate
  assign controlled_buffer_1_out = in_6 ? in_5 : 16'bz;  // Controlled_Buffer controlled_buffer_4
  assign controlled_buffer_1_out = in_9 ? multiplexer_1_out : 16'bz;  // Controlled_Buffer controlled_buffer_5
  not not_1 (not_1_out, in_9);
  assign bit_extender_1_out = {{16{1'b0}}, controlled_buffer_1_out};  // Bit_Extender bit_extender_1
  Multiplexer #(.width(32), .enable("false")) multiplexer_2 (
    .in0(bit_extender_1_out), .in1(in_7), .out(out_14), .sel(in_8));
endmodule

module uc (
  input  in_1,
  input  in_2,
  input  in_3,
  input  in_4,
  input  in_5,
  input  in_6,
  input  in_7,
  output input_pin,
  output input_sum,
  output out_10,
  output enable_retragere,
  output enable_afis,
  output out_13,
  output out_14,
  output out_15,
  output alege_optiune
);

  wire and_1_out, and_2_out, and_3_out, comparator_1_eq, counter_1_q, counter_2_carry, demultiplexer_1_out0,
       demultiplexer_1_out4, demultiplexer_1_out5, demultiplexer_1_out6, demultiplexer_1_out8,
       demultiplexer_1_out9, demultiplexer_1_out10, not_1_out, not_2_out;
  wire [3:0] controlled_buffer_1_out, multiplexer_1_out, multiplexer_2_out, multiplexer_3_out,
       multiplexer_4_out, multiplexer_5_out, register_1_q;

  Multiplexer #(.width(4), .enable("false")) multiplexer_1 (
    .in0(4'b0101), .in1(4'b0011), .out(multiplexer_1_out), .sel(in_4));
  and and_1 (and_1_out, in_7, enable_afis);
  Multiplexer #(.select(2), .width(4), .enable("false")) multiplexer_2 (
    .in0(4'b0111), .in1(4'b0011), .in2(4'b0011), .out(multiplexer_2_out), .sel({in_6, in_4}));  // open: in3
  Multiplexer #(.select(2), .width(4), .enable("false")) multiplexer_3 (
    .in0(4'b1010), .in1(4'b0011), .in2(4'b0011), .out(multiplexer_3_out), .sel({in_6, in_4}));  // open: in3
  Counter #(.width(1), .max('h1), .ongoal("stay")) counter_1 (
    .count(in_3), .Q(counter_1_q), .clk(in_3), .clr(not_2_out));  // open: load, D, carry
  Multiplexer #(.width(4), .enable("false")) multiplexer_4 (
    .in0(4'b0000), .in1(4'b0001), .out(multiplexer_4_out), .sel(counter_1_q));
  Register #(.width(4)) register_1 (
    .D(controlled_buffer_1_out), .en(and_1_out), .Q(register_1_q), .clk(and_1_out));  // open: clr
  not not_1 (not_1_out, counter_1_q);
  and and_2 (and_2_out, not_1_out, and_1_out);
  assign controlled_buffer_1_out = enable_retragere ? multiplexer_2_out : 4'bz;  // Controlled_Buffer controlled_buffer_1
  Comparator #(.width(4), .mode("unsigned")) comparator_1 (
    .a(4'b0011), .b(register_1_q), .eq(comparator_1_eq));  // open: gt, lt
  Counter #(.width(1), .max('h1), .ongoal("stay")) counter_2 (
    .count(comparator_1_eq), .carry(counter_2_carry), .clk(and_1_out), .clr(not_2_out));  // open: load, D, Q
  not not_2 (not_2_out, comparator_1_eq);
  and and_3 (and_3_out, counter_2_carry, and_2_out);
  Demultiplexer #(.select(4), .enable("false")) demultiplexer_1 (
    .out0(demultiplexer_1_out0), .out1(alege_optiune), .out2(out_14), .out3(out_15),
    .out4(demultiplexer_1_out4), .out5(demultiplexer_1_out5), .out6(demultiplexer_1_out6),
    .out7(enable_retragere), .out8(demultiplexer_1_out8), .out9(demultiplexer_1_out9),
    .out10(demultiplexer_1_out10), .in(1'b1), .sel(register_1_q));  // open: out11, out12, out13, out14, out15
  assign controlled_buffer_1_out = out_15 ? multiplexer_4_out : 4'bz;  // Controlled_Buffer controlled_buffer_2
  assign controlled_buffer_1_out = demultiplexer_1_out6 ? 4'b0111 : 4'bz;  // Controlled_Buffer controlled_buffer_3
  assign controlled_buffer_1_out = alege_optiune ? multiplexer_5_out : 4'bz;  // Controlled_Buffer controlled_buffer_4
  assign controlled_buffer_1_out = demultiplexer_1_out5 ? multiplexer_1_out : 4'bz;  // Controlled_Buffer controlled_buffer_5
  Multiplexer #(.select(2), .width(4), .enable("false")) multiplexer_5 (
    .in0(4'b0010), .in1(4'b0100), .in2(4'b0110), .in3(4'b1000), .out(multiplexer_5_out), .sel({in_1, in_2}));
  assign controlled_buffer_1_out = out_14 ? 4'b0011 : 4'bz;  // Controlled_Buffer controlled_buffer_6
  assign controlled_buffer_1_out = demultiplexer_1_out4 ? 4'b0101 : 4'bz;  // Controlled_Buffer controlled_buffer_7
  assign controlled_buffer_1_out = demultiplexer_1_out9 ? 4'b1010 : 4'bz;  // Controlled_Buffer controlled_buffer_8
  assign controlled_buffer_1_out = demultiplexer_1_out8 ? 4'b1001 : 4'bz;  // Controlled_Buffer controlled_buffer_9
  assign controlled_buffer_1_out = demultiplexer_1_out10 ? multiplexer_3_out : 4'bz;  // Controlled_Buffer controlled_buffer_10
  assign controlled_buffer_1_out = demultiplexer_1_out0 ? 4'b0001 : 4'bz;  // Controlled_Buffer controlled_buffer_11
  or or_1 (input_pin, demultiplexer_1_out0, demultiplexer_1_out8);
  or or_2 (out_10, demultiplexer_1_out5, demultiplexer_1_out4);
  or or_3 (out_13, demultiplexer_1_out8, demultiplexer_1_out10, demultiplexer_1_out9);
  or or_4 (input_sum, demultiplexer_1_out9, demultiplexer_1_out6);
  Counter #(.width(1), .max('h1), .ongoal("stay")) counter_3 (
    .count(in_5), .Q(enable_afis), .clk(in_5), .clr(and_3_out));  // open: load, D, carry

  // Notes on the sheet:
  //   enable depunere
  //   enable transfer
  //   enable interogare
endmodule

module BANCOMAT (
  input  in_1,
  input  in_2,
  input  p3,
  input  p2,
  input  p1,
  input  p0,
  input  reset,
  input  s,
  input  z,
  input  u,
  input  _500,
  input  _200,
  input  _100,
  input  _50,
  input  _10,
  input  _5,
  input  in_17,
  input  confirm,
  input  in_19,
  input  next,
  output finish,
  output fail,
  output [7:0] out_23,
  output [6:0] out_24
);

  wire and_1_out, and_2_out, and_3_out, counter_1_carry, counter_2_carry, counter_3_carry, counter_4_carry,
       depunere_1_out_19, depunere_1_store_banc, depunere_1_store_cont, multiplexer_5_out, multiplexer_8_out,
       multiplexer_9_out, multiplexer_10_out, multiplexer_11_out, not_1_out, not_2_out, not_3_out, or_2_out,
       or_3_out, or_4_out, or_5_out, retragere_1_out_8, retragere_1_out_9, transfer_1_failed,
       transfer_1_finished, transfer_1_out_11, uc_1_alege_optiune, uc_1_enable_afis, uc_1_enable_retragere,
       uc_1_input_pin, uc_1_input_sum, uc_1_out_10, uc_1_out_13, uc_1_out_14, uc_1_out_15;
  wire [3:0] controlled_buffer_3_out, controlled_buffer_4_out, counter_4_q, depunere_1_out_16,
       inputpin_1_out_7, multiplexer_1_out, multiplexer_2_out, multiplexer_4_out, multiplexer_7_out,
       register_1_q, retragere_1_out_10, transfer_1_out_7;
  wire [15:0] controlled_buffer_1_out, controlled_buffer_2_out, depunere_1_cont_out, depunere_1_out_13,
       depunere_1_out_17, inputpin_1_out_8, inputsum_1_out_8, inputsum_1_out_9, multiplexer_3_out,
       multiplexer_6_out, ram_1_data, ram_2_data, retragere_1_out_7, retragere_1_out_11, transfer_1_out_8;
  wire [31:0] retragere_1_out_6, selectie_afisor_1_out_14;

  uc uc_1 (
    .in_3(reset), .in_4(finish), .in_6(fail), .in_7(confirm), .input_pin(uc_1_input_pin),
    .input_sum(uc_1_input_sum), .out_10(uc_1_out_10), .enable_retragere(uc_1_enable_retragere),
    .enable_afis(uc_1_enable_afis), .out_13(uc_1_out_13), .out_14(uc_1_out_14),
    .alege_optiune(uc_1_alege_optiune), .in_1(in_1), .in_2(in_2), .in_5(in_17), .out_15(uc_1_out_15));
  and and_1 (and_1_out, not_2_out, confirm);
  inputPIN inputpin_1 (
    .enable(uc_1_input_pin), .out_7(inputpin_1_out_7), .out_8(inputpin_1_out_8), .in_1(p3), .in_2(p2),
    .in_3(p1), .in_4(p0), .confirm(confirm));
  Counter #(.width(2), .max('h2), .ongoal("stay")) counter_1 (
    .count(confirm), .carry(counter_1_carry), .clk(confirm), .clr(not_1_out));  // open: load, D, Q
  not not_1 (not_1_out, uc_1_enable_afis);
  not not_2 (not_2_out, counter_1_carry);
  Register #(.width(4)) register_1 (.D(inputpin_1_out_7), .en(and_1_out), .Q(register_1_q), .clk(in_19));  // open: clr
  Counter #(.width(1), .max('h1), .ongoal("stay")) counter_2 (
    .count(uc_1_out_13), .carry(counter_2_carry), .clk(in_19), .clr(not_3_out));  // open: load, D, Q
  inputSum inputsum_1 (
    .confirm(confirm), .enable(uc_1_input_sum), .out_8(inputsum_1_out_8), .out_9(inputsum_1_out_9), .in_1(s),
    .in_2(z), .in_3(u), .clock(in_19), .next(next));
  depunere depunere_1 (
    .in_7(ram_2_data), .in_8(uc_1_out_10), .in_9(reset), .in_10(ram_1_data), .in_11(confirm),
    .cont_out(depunere_1_cont_out), .store_cont(depunere_1_store_cont), .out_16(depunere_1_out_16),
    .out_17(depunere_1_out_17), .store_banc(depunere_1_store_banc), .out_19(depunere_1_out_19), .in_1(_500),
    .in_2(_200), .in_3(_100), .in_4(_50), .in_5(_10), .in_6(_5), .out_13(depunere_1_out_13), .in_12(in_19));
  Multiplexer #(.width(4), .enable("false")) multiplexer_1 (
    .in0(register_1_q), .in1(inputpin_1_out_7), .out(multiplexer_1_out), .sel(uc_1_out_13));
  not not_3 (not_3_out, uc_1_out_13);
  Counter #(.width(1), .max('h1), .ongoal("stay")) counter_3 (
    .count(in_17), .carry(counter_3_carry), .clk(in_17));  // open: load, D, Q, clr
  Counter #(.width(4), .max('h6), .ongoal("stay")) counter_4 (
    .count(counter_3_carry), .Q(counter_4_q), .carry(counter_4_carry), .clk(in_19));  // open: load, D, clr
  Multiplexer #(.width(4), .enable("false")) multiplexer_2 (
    .in0(register_1_q), .in1(multiplexer_1_out), .out(multiplexer_2_out), .sel(counter_2_carry));
  or or_1 (finish, depunere_1_out_19, or_5_out);
  or or_2 (or_2_out, uc_1_enable_retragere, uc_1_out_14, uc_1_out_10);
  assign controlled_buffer_1_out = uc_1_out_10 ? depunere_1_cont_out : 16'bz;  // Controlled_Buffer controlled_buffer_1
  assign controlled_buffer_2_out = uc_1_out_10 ? depunere_1_out_17 : 16'bz;  // Controlled_Buffer controlled_buffer_2
  Multiplexer #(.width(16), .enable("false")) multiplexer_3 (
    .in0(16'ha), .in1(controlled_buffer_2_out), .out(multiplexer_3_out), .sel(counter_4_carry));
  Multiplexer #(.width(4), .enable("false")) multiplexer_4 (
    .in0(counter_4_q), .in1(controlled_buffer_4_out), .out(multiplexer_4_out), .sel(counter_4_carry));
  Multiplexer #(.enable("false")) multiplexer_5 (
    .in0(1'b1), .in1(and_2_out), .out(multiplexer_5_out), .sel(counter_4_carry));
  selectie_afisor selectie_afisor_1 (
    .in_1(inputpin_1_out_8), .in_2(uc_1_input_pin), .in_3(inputsum_1_out_8), .in_4(uc_1_input_sum),
    .in_5(depunere_1_out_13), .in_6(uc_1_out_10), .in_7(retragere_1_out_6), .in_8(uc_1_enable_retragere),
    .in_9(uc_1_out_13), .in_11(ram_2_data), .in_12(uc_1_out_14), .in_13(confirm),
    .out_14(selectie_afisor_1_out_14), .in_10(in_19));
  assign controlled_buffer_3_out = or_2_out ? multiplexer_1_out : 4'bz;  // Controlled_Buffer controlled_buffer_3
  RAM #(.addrWidth(4), .dataWidth(16), .bus("separate")) ram_1 (
    .addr(multiplexer_4_out), .din(multiplexer_3_out), .data(ram_1_data), .str(multiplexer_5_out),
    .sel(1'b1), .clk(in_19), .ld(1'b1));  // open: clr
  or or_3 (or_3_out, uc_1_out_10, uc_1_out_13, uc_1_enable_retragere);
  Multiplexer #(.width(16), .enable("false")) multiplexer_6 (
    .in0(16'haaa), .in1(controlled_buffer_1_out), .out(multiplexer_6_out), .sel(counter_4_carry));
  Multiplexer #(.width(4), .enable("false")) multiplexer_7 (
    .in0(counter_4_q), .in1(controlled_buffer_3_out), .out(multiplexer_7_out), .sel(counter_4_carry));
  Multiplexer #(.enable("false")) multiplexer_8 (
    .in0(1'b1), .in1(depunere_1_store_banc), .out(multiplexer_8_out), .sel(uc_1_out_10));
  Multiplexer #(.enable("false")) multiplexer_9 (
    .in0(1'b1), .in1(depunere_1_store_cont), .out(multiplexer_9_out), .sel(uc_1_out_10));
  afisor afisor_1 (
    .out_7(out_24), .out_8(out_23), .in_1(selectie_afisor_1_out_14), .in_2(uc_1_enable_afis), .in_3(in_19),
    .in_4(uc_1_enable_retragere), .in_5(uc_1_alege_optiune), .in_6(uc_1_out_15));
  or or_4 (or_4_out, uc_1_enable_retragere, uc_1_out_10);
  retragere retragere_1 (
    .in_1(inputsum_1_out_9), .in_2(ram_2_data), .in_3(uc_1_enable_retragere), .in_4(in_19),
    .out_7(retragere_1_out_7), .out_8(retragere_1_out_8), .out_9(retragere_1_out_9),
    .out_11(retragere_1_out_11), .in_5(ram_1_data), .out_10(retragere_1_out_10), .out_6(retragere_1_out_6));
  assign controlled_buffer_4_out = uc_1_enable_retragere ? retragere_1_out_10 : 4'bz;  // Controlled_Buffer controlled_buffer_4
  assign controlled_buffer_4_out = uc_1_out_10 ? depunere_1_out_16 : 4'bz;  // Controlled_Buffer controlled_buffer_5
  RAM #(.addrWidth(4), .dataWidth(16), .bus("separate")) ram_2 (
    .addr(multiplexer_7_out), .din(multiplexer_6_out), .data(ram_2_data), .str(multiplexer_10_out),
    .sel(1'b1), .clk(in_19), .ld(1'b1));  // open: clr
  and and_2 (and_2_out, multiplexer_8_out, or_4_out);
  and and_3 (and_3_out, multiplexer_9_out, or_3_out);
  Multiplexer #(.enable("false")) multiplexer_10 (
    .in0(1'b1), .in1(multiplexer_11_out), .out(multiplexer_10_out), .sel(counter_4_carry));
  Multiplexer #(.enable("false")) multiplexer_11 (
    .in0(and_3_out), .in1(transfer_1_out_11), .out(multiplexer_11_out), .sel(uc_1_out_13));
  assign controlled_buffer_1_out = uc_1_enable_retragere ? retragere_1_out_7 : 16'bz;  // Controlled_Buffer controlled_buffer_6
  assign controlled_buffer_2_out = uc_1_enable_retragere ? retragere_1_out_11 : 16'bz;  // Controlled_Buffer controlled_buffer_7
  assign controlled_buffer_3_out = uc_1_out_13 ? transfer_1_out_7 : 4'bz;  // Controlled_Buffer controlled_buffer_8
  or or_5 (or_5_out, transfer_1_finished, retragere_1_out_9);
  assign controlled_buffer_1_out = uc_1_out_13 ? transfer_1_out_8 : 16'bz;  // Controlled_Buffer controlled_buffer_9
  or or_6 (fail, transfer_1_failed, retragere_1_out_8);
  transfer transfer_1 (
    .PIN(multiplexer_2_out), .Confim(confirm), .Suma(inputsum_1_out_9), .Enable(uc_1_out_13),
    .Failed(transfer_1_failed), .Finished(transfer_1_finished), .in_2(ram_2_data), .out_7(transfer_1_out_7),
    .out_8(transfer_1_out_8), .in_6(in_19), .out_11(transfer_1_out_11));
endmodule
